# Fritzing sketch Party Traffic Light (saved by Fritzing 0.9.4)
breadboards: 2

parts:
  LED1 = LED - 5mm [color="Red (633nm)" package="5 mm [THT]"]
  LED2 = LED - 5mm [color="Green (570nm)" package="5 mm [THT]"]
  LED3 = LED - 5mm [color="Yellow (595nm)" package="5 mm [THT]"]
  Part1 = Arduino Uno (Rev3)
  J1 = Piezo Speaker  # not connected
  SP1 = SPEAKER [package=pcb_mount_speaker]
  R1 = Resistor [tolerance=±5% resistance=100 package="2512 [SMD]"]
  R2 = Resistor [tolerance=±5% resistance=100 package="2512 [SMD]"]
  R3 = Resistor [tolerance=±5% resistance=100 package="2512 [SMD]"]
  LED4 = LED - 5mm [color="Red (633nm)" package="5 mm [THT]"]
  LED5 = LED - 5mm [color="Yellow (595nm)" package="5 mm [THT]"]
  LED6 = LED - 5mm [color="Green (570nm)" package="5 mm [THT]"]
  R4 = Resistor [tolerance=±5% resistance=100 package="2512 [SMD]"]
  R5 = Resistor [tolerance=±5% resistance=100 package="2512 [SMD]"]
  R6 = Resistor [tolerance=±5% resistance=100 package="2512 [SMD]"]

nets:
  N1: LED1.cathode, R3.Pin_0
  N2: LED1.anode, LED2.anode, LED3.anode, Part1.GND, SP1.+, LED4.anode, LED5.anode, LED6.anode
  N3: LED2.cathode, R1.Pin_0
  N4: LED3.cathode, R2.Pin_0
  N5: Part1.D8, SP1.-
  N6: Part1.D9_PWM, R5.Pin_1
  N7: Part1.D10_PWM/SS, R6.Pin_1
  N8: Part1.D11_PWM/MOSI, R4.Pin_1
  N9: Part1.D3_PWM, R1.Pin_1
  N10: Part1.D5_PWM, R2.Pin_1
  N11: Part1.D6_PWM, R3.Pin_1
  N12: LED4.cathode, R4.Pin_0
  N13: LED5.cathode, R6.Pin_0
  N14: LED6.cathode, R5.Pin_0

notes:
  PIEZO OR SPEAKER
